// Logisim project procesadorarm.circ as structural Verilog: 3 circuits, main circuit main
module main (
);

  REGFILE regfile_1 ();  // open: _2c, H, L, _1c, MAR, read_onoff, salida
  ALU alu_1 ();  // open: A_h, A_l, in_3, in_4, B_h, B_l, alta, baja
endmodule

module ALU (
  input  [31:0] A_h,
  input  [31:0] A_l,
  input  in_3,
  input  [1:0] in_4,
  input  [31:0] B_h,
  input  [31:0] B_l,
  output [31:0] alta,
  output [31:0] baja
);

  wire adder_1_cout, adder_2_cout;
  wire [31:0] adder_1_out, adder_2_out, and_1_out, and_2_out, multiplier_1_out, multiplier_2_out, or_1_out,
       or_2_out;

  assign and_1_out = A_h & B_h;  // AND_Gate and_1, 32 bits wide
  Adder #(.width(32)) adder_1 (.a(A_h), .b(B_h), .out(adder_1_out), .cin(adder_2_cout), .cout(adder_1_cout));
  Multiplier #(.width(32)) multiplier_1 (.a(A_h), .b(B_h), .out(multiplier_1_out));  // open: cin, cout
  assign or_1_out = A_h | B_h;  // OR_Gate or_1, 32 bits wide
  assign and_2_out = A_l & A_l;  // AND_Gate and_2, 32 bits wide
  Adder #(.width(32)) adder_2 (.a(A_l), .b(B_l), .out(adder_2_out), .cin(adder_1_cout), .cout(adder_2_cout));
  Multiplier #(.width(32)) multiplier_2 (.a(A_l), .b(B_l), .out(multiplier_2_out));  // open: cin, cout
  assign or_2_out = A_l | B_l;  // OR_Gate or_2, 32 bits wide
  Multiplexer #(.select(2), .width(32)) multiplexer_1 (
    .in0(and_1_out), .in1(adder_1_out), .in2(multiplier_1_out), .in3(or_1_out), .out(alta), .sel(in_4),
    .en(in_3));
  Multiplexer #(.select(2), .width(32)) multiplexer_2 (
    .in0(and_2_out), .in1(adder_2_out), .in2(multiplier_2_out), .in3(or_2_out), .out(baja), .sel(in_4),
    .en(in_3));
endmodule

module REGFILE (
  input  _2c,
  input  [31:0] H,
  input  [31:0] L,
  input  _1c,
  input  [4:0] MAR,
  input  read_onoff,
  output salida
);

  wire [31:0] and_1_out, demultiplexer_1_out0, demultiplexer_1_out1, demultiplexer_1_out2,
       demultiplexer_1_out3, demultiplexer_1_out4, demultiplexer_1_out5, demultiplexer_1_out6,
       demultiplexer_1_out7, demultiplexer_1_out8, demultiplexer_1_out9, demultiplexer_1_out10,
       demultiplexer_1_out11, demultiplexer_1_out12, demultiplexer_1_out13, demultiplexer_1_out14,
       demultiplexer_1_out15, demultiplexer_1_out16, demultiplexer_1_out17, demultiplexer_1_out18,
       demultiplexer_1_out19, demultiplexer_1_out20, demultiplexer_1_out21, demultiplexer_1_out22,
       demultiplexer_1_out23, demultiplexer_1_out24, demultiplexer_1_out25, demultiplexer_1_out26,
       demultiplexer_1_out27, demultiplexer_1_out28, demultiplexer_1_out29, demultiplexer_1_out30,
       demultiplexer_1_out31, multiplexer_1_out, x0_q, x1_q, x2_q, x3_q, x4_q, x5_q, x6_q, x7_q, x8_q, x9_q,
       x10_q, x11_q, x12_q, x13_q, x14_q, x15_q, x16_q, x17_q, x18_q, x19_q, x20_q, x21_q, x22_q, x23_q,
       x24_q, x25_q, x26_q, x27_q, x28_q, x29_q, x30_q, x31_q;

  assign and_1_out = H & L;  // AND_Gate and_1, 32 bits wide
  Demultiplexer #(.select(5), .width(32)) demultiplexer_1 (
    .out0(demultiplexer_1_out0), .out1(demultiplexer_1_out1), .out2(demultiplexer_1_out2),
    .out3(demultiplexer_1_out3), .out4(demultiplexer_1_out4), .out5(demultiplexer_1_out5),
    .out6(demultiplexer_1_out6), .out7(demultiplexer_1_out7), .out8(demultiplexer_1_out8),
    .out9(demultiplexer_1_out9), .out10(demultiplexer_1_out10), .out11(demultiplexer_1_out11),
    .out12(demultiplexer_1_out12), .out13(demultiplexer_1_out13), .out14(demultiplexer_1_out14),
    .out15(demultiplexer_1_out15), .out16(demultiplexer_1_out16), .out17(demultiplexer_1_out17),
    .out18(demultiplexer_1_out18), .out19(demultiplexer_1_out19), .out20(demultiplexer_1_out20),
    .out21(demultiplexer_1_out21), .out22(demultiplexer_1_out22), .out23(demultiplexer_1_out23),
    .out24(demultiplexer_1_out24), .out25(demultiplexer_1_out25), .out26(demultiplexer_1_out26),
    .out27(demultiplexer_1_out27), .out28(demultiplexer_1_out28), .out29(demultiplexer_1_out29),
    .out30(demultiplexer_1_out30), .out31(demultiplexer_1_out31), .in(and_1_out), .sel(MAR), .en(_1c));
  Register #(.width(32)) x0 (.D(demultiplexer_1_out0), .Q(x0_q), .clk(_2c));  // open: en, clr
  Register #(.width(32)) x1 (.D(demultiplexer_1_out1), .Q(x1_q), .clk(_2c));  // open: en, clr
  Register #(.width(32)) x2 (.D(demultiplexer_1_out2), .Q(x2_q), .clk(_2c));  // open: en, clr
  Register #(.width(32)) x3 (.D(demultiplexer_1_out3), .Q(x3_q), .clk(_2c));  // open: en, clr
  Register #(.width(32)) x4 (.D(demultiplexer_1_out4), .Q(x4_q), .clk(_2c));  // open: en, clr
  Register #(.width(32)) x5 (.D(demultiplexer_1_out5), .Q(x5_q), .clk(_2c));  // open: en, clr
  Register #(.width(32)) x6 (.D(demultiplexer_1_out6), .Q(x6_q), .clk(_2c));  // open: en, clr
  Register #(.width(32)) x7 (.D(demultiplexer_1_out7), .Q(x7_q), .clk(_2c));  // open: en, clr
  Register #(.width(32)) x8 (.D(demultiplexer_1_out8), .Q(x8_q), .clk(_2c));  // open: en, clr
  Register #(.width(32)) x9 (.D(demultiplexer_1_out9), .Q(x9_q), .clk(_2c));  // open: en, clr
  Register #(.width(32)) x10 (.D(demultiplexer_1_out10), .Q(x10_q), .clk(_2c));  // open: en, clr
  Register #(.width(32)) x11 (.D(demultiplexer_1_out11), .Q(x11_q), .clk(_2c));  // open: en, clr
  Register #(.width(32)) x12 (.D(demultiplexer_1_out12), .Q(x12_q), .clk(_2c));  // open: en, clr
  Register #(.width(32)) x13 (.D(demultiplexer_1_out13), .Q(x13_q), .clk(_2c));  // open: en, clr
  Register #(.width(32)) x14 (.D(demultiplexer_1_out14), .Q(x14_q), .clk(_2c));  // open: en, clr
  Register #(.width(32)) x15 (.D(demultiplexer_1_out15), .Q(x15_q), .clk(_2c));  // open: en, clr
  Register #(.width(32)) x16 (.D(demultiplexer_1_out16), .Q(x16_q), .clk(_2c));  // open: en, clr
  Register #(.width(32)) x17 (.D(demultiplexer_1_out17), .Q(x17_q), .clk(_2c));  // open: en, clr
  Register #(.width(32)) x18 (.D(demultiplexer_1_out18), .Q(x18_q), .clk(_2c));  // open: en, clr
  Register #(.width(32)) x19 (.D(demultiplexer_1_out19), .Q(x19_q), .clk(_2c));  // open: en, clr
  Register #(.width(32)) x20 (.D(demultiplexer_1_out20), .Q(x20_q), .clk(_2c));  // open: en, clr
  Register #(.width(32)) x21 (.D(demultiplexer_1_out21), .Q(x21_q), .clk(_2c));  // open: en, clr
  Register #(.width(32)) x22 (.D(demultiplexer_1_out22), .Q(x22_q), .clk(_2c));  // open: en, clr
  Register #(.width(32)) x23 (.D(demultiplexer_1_out23), .Q(x23_q), .clk(_2c));  // open: en, clr
  Register #(.width(32)) x24 (.D(demultiplexer_1_out24), .Q(x24_q), .clk(_2c));  // open: en, clr
  Register #(.width(32)) x25 (.D(demultiplexer_1_out25), .Q(x25_q), .clk(_2c));  // open: en, clr
  Register #(.width(32)) x26 (.D(demultiplexer_1_out26), .Q(x26_q), .clk(_2c));  // open: en, clr
  Register #(.width(32)) x27 (.D(demultiplexer_1_out27), .Q(x27_q), .clk(_2c));  // open: en, clr
  Register #(.width(32)) x28 (.D(demultiplexer_1_out28), .Q(x28_q), .clk(_2c));  // open: en, clr
  Register #(.width(32)) x29 (.D(demultiplexer_1_out29), .Q(x29_q), .clk(_2c));  // open: en, clr
  Register #(.width(32)) x30 (.D(demultiplexer_1_out30), .Q(x30_q), .clr(_2c));  // open: en, clk
  Register #(.width(32)) x31 (.D(demultiplexer_1_out31), .Q(x31_q), .clk(_2c));  // open: en, clr
  Multiplexer #(.select(5), .width(32)) multiplexer_1 (
    .in0(x0_q), .in1(x1_q), .in2(x2_q), .in3(x3_q), .in4(x4_q), .in5(x5_q), .in6(x6_q), .in7(x7_q),
    .in8(x8_q), .in9(x9_q), .in10(x10_q), .in11(x11_q), .in12(x12_q), .in13(x13_q), .in14(x14_q),
    .in15(x15_q), .in16(x16_q), .in17(x17_q), .in18(x18_q), .in19(x19_q), .in20(x20_q), .in21(x21_q),
    .in22(x22_q), .in23(x23_q), .in24(x24_q), .in25(x25_q), .in26(x26_q), .in27(x27_q), .in28(x28_q),
    .in29(x29_q), .in30(x30_q), .in31(x31_q), .out(multiplexer_1_out), .sel(MAR), .en(read_onoff));
  Multiplexer #(.select(5), .width(32)) multiplexer_2 ();  // open: in0, in1, in2, in3, in4, in5, in6, in7, in8, in9, in10, in11, in12, in13, in14, in15, in16, in17, in18, in19, in20, in21, in22, in23, in24, in25, in26, in27, in28, in29, in30, in31, out, sel, en
endmodule
