// Logisim project process.circ as structural Verilog: 7 circuits, main circuit main
module main (
  input  in_1,
  input  Clk,
  input  in_3,
  input  in_4,
  input  in_5,
  output [15:0] out_6,
  output [15:0] out_7,
  output [15:0] out_8,
  output [15:0] out_9
);

  wire branch, branchbit, clock, clock_1_out, comparator_1_eq, comparator_2_eq, comparator_3_eq,
       comparator_4_eq, comparator_5_eq, multiplexer_2_out, multiplexer_3_out, not_1_out, not_2_out;
  wire [3:0] guar, opc, reg_2;
  wire [15:0] adder_1_out, alu_1_reg_dest, brnach_1_salida, dest, jump_1_salida, multiplexer_1_out, pc,
       ram_2_data;
  wire [15:8] ram;

  Adder #(.width(16)) adder_1 (.a(pc), .b(16'h1), .out(adder_1_out));  // open: cin, cout
  jump jump_1 (.ram({ram, guar, opc}), .pc(adder_1_out), .\reg (out_9), .sal_reg(reg_2), .salida(jump_1_salida));
  Comparator #(.width(3)) comparator_1 (.a(opc[3:1]), .b(3'b100), .eq(comparator_1_eq));  // open: gt, lt
  Multiplexer #(.width(16)) multiplexer_1 (
    .in0(out_9), .in1(dest), .out(multiplexer_1_out), .sel(multiplexer_3_out));  // open: en
  assign clock = in_3 ? Clk : 1'bz;  // Controlled_Buffer controlled_buffer_1
  not not_1 (not_1_out, in_3);
  brnach brnach_1 (.inm({ram, guar, opc}), .pc(pc), .sum(jump_1_salida), .bitbranch(branch), .salida(brnach_1_salida));
  Register #(.width(16)) u_PC (.D(brnach_1_salida), .Q(pc), .clk(clock), .clr(in_4));  // open: en
  registros registros_1 (
    .reg_guar(dest), .\var (in_1), .dest(guar), .eleg_reg_2(reg_2), .on_off(in_1), .eleg_reg_1(ram[11:8]),
    .cloc(clock), .reg_1(out_6), .reg_2(out_9));
  assign clock = not_1_out ? clock_1_out : 1'bz;  // Controlled_Buffer controlled_buffer_2
  Clock clock_1 (.out(clock_1_out));
  Multiplexer multiplexer_2 (.in0(clock), .in1(in_1), .out(multiplexer_2_out), .sel(multiplexer_3_out));  // open: en
  cambio cambio_1 (.entrada(ram_2_data), .out_2({ram, guar, opc}));
  RAM #(.addrWidth(16), .dataWidth(16), .bus("separate")) ram_1 (
    .addr(out_6), .din(multiplexer_1_out), .data(dest), .str(multiplexer_2_out), .sel(comparator_1_eq),
    .clk(multiplexer_2_out), .ld(multiplexer_3_out));  // open: clr
  RAM #(.addrWidth(16), .dataWidth(16)) ram_2 (
    .addr(pc), .data(ram_2_data), .sel(in_1), .clk(clock), .ld(in_1));  // open: clr
  Comparator #(.width(4)) comparator_2 (.a(opc), .b(4'b1001), .eq(comparator_2_eq));  // open: gt, lt
  Multiplexer multiplexer_3 (.in0(in_5), .in1(opc[0]), .out(multiplexer_3_out), .sel(comparator_2_eq));  // open: en
  lilui lilui_1 (.entrada({ram, guar, opc}), .imedia(dest));
  Hex_Digit_Display hex_digit_display_1 (.value(opc));  // open: dp
  Comparator #(.width(4)) comparator_3 (.a(4'b1111), .b(opc), .eq(comparator_3_eq));  // open: gt, lt
  Multiplexer #(.width(16)) multiplexer_4 (.in0(dest), .in1(dest), .en(opc[0]));  // open: out, sel
  Comparator #(.width(4)) comparator_4 (.a(opc), .b(4'b1001), .eq(comparator_4_eq));  // open: gt, lt
  Comparator #(.width(4)) comparator_5 (.a(opc), .b(4'b1110), .eq(comparator_5_eq));  // open: gt, lt
  Hex_Digit_Display hex_digit_display_2 (.value(guar));  // open: dp
  Multiplexer #(.width(16)) multiplexer_5 (.in1(pc), .out(dest), .sel(comparator_3_eq));  // open: in0, en
  ALU alu_1 (.reg_A(out_6), .Reg_B(out_8), .off_on({ram, guar, opc}), .Reg_Dest(alu_1_reg_dest), .BRANHC(branchbit));
  assign dest = not_2_out ? alu_1_reg_dest : 16'bz;  // Controlled_Buffer controlled_buffer_3
  not not_2 (not_2_out, comparator_4_eq);
  Multiplexer #(.width(4)) multiplexer_6 (.in0(ram[15:12]), .out(reg_2), .sel(comparator_5_eq));  // open: in1, en
  Hex_Digit_Display hex_digit_display_3 (.value(ram[11:8]));  // open: dp
  Hex_Digit_Display hex_digit_display_4 (.value(ram[15:12]));  // open: dp
  Register #(.width(1)) register_1 (.D(branchbit), .en(in_1), .Q(branch), .clk(clock));  // open: clr

  assign out_7 = out_6;

  // Other names for the same wires on the sheet: _1 = in_1; ram[7:0] = {guar, opc}; selec = opc[0];
  //   reg_1[3:0] = ram[11:8]; val_1[15:0] = out_6; val_2[15:0] = out_9; val_2_t[15:0] = out_8

  // Notes on the sheet:
  //   opcode
endmodule

module registros (
  input  [15:0] reg_guar,
  input  \var ,
  input  [3:0] dest,
  input  [3:0] eleg_reg_2,
  input  on_off,
  input  [3:0] eleg_reg_1,
  input  cloc,
  output [15:0] reg_1,
  output [15:0] reg_2
);

  wire demultiplexer_1_out1, demultiplexer_1_out2, demultiplexer_1_out3, demultiplexer_1_out4,
       demultiplexer_1_out5, demultiplexer_1_out6, demultiplexer_1_out7, demultiplexer_1_out8,
       demultiplexer_1_out9, demultiplexer_1_out10, demultiplexer_1_out11, demultiplexer_1_out12,
       demultiplexer_1_out13, demultiplexer_1_out14, demultiplexer_1_out15;
  wire [15:0] register_1_q, register_2_q, register_3_q, register_4_q, register_5_q, register_6_q,
       register_7_q, register_8_q, register_9_q, register_10_q, register_11_q, register_12_q, register_13_q,
       register_14_q, register_15_q;

  Demultiplexer #(.select(4), .disabled(0)) demultiplexer_1 (
    .out1(demultiplexer_1_out1), .out2(demultiplexer_1_out2), .out3(demultiplexer_1_out3),
    .out4(demultiplexer_1_out4), .out5(demultiplexer_1_out5), .out6(demultiplexer_1_out6),
    .out7(demultiplexer_1_out7), .out8(demultiplexer_1_out8), .out9(demultiplexer_1_out9),
    .out10(demultiplexer_1_out10), .out11(demultiplexer_1_out11), .out12(demultiplexer_1_out12),
    .out13(demultiplexer_1_out13), .out14(demultiplexer_1_out14), .out15(demultiplexer_1_out15), .in(1'b1),
    .sel(dest), .en(\var ));  // open: out0
  Register #(.width(16)) register_1 (
    .D(reg_guar), .en(demultiplexer_1_out1), .Q(register_1_q), .clk(cloc));  // open: clr
  Register #(.width(16)) register_2 (
    .D(reg_guar), .en(demultiplexer_1_out2), .Q(register_2_q), .clk(cloc));  // open: clr
  Register #(.width(16)) register_3 (
    .D(reg_guar), .en(demultiplexer_1_out3), .Q(register_3_q), .clk(cloc));  // open: clr
  Register #(.width(16)) register_4 (
    .D(reg_guar), .en(demultiplexer_1_out4), .Q(register_4_q), .clk(cloc));  // open: clr
  Register #(.width(16)) register_5 (
    .D(reg_guar), .en(demultiplexer_1_out5), .Q(register_5_q), .clk(cloc));  // open: clr
  Register #(.width(16)) register_6 (
    .D(reg_guar), .en(demultiplexer_1_out6), .Q(register_6_q), .clk(cloc));  // open: clr
  Register #(.width(16)) register_7 (
    .D(reg_guar), .en(demultiplexer_1_out7), .Q(register_7_q), .clk(cloc));  // open: clr
  Register #(.width(16)) register_8 (
    .D(reg_guar), .en(demultiplexer_1_out9), .Q(register_8_q), .clk(cloc));  // open: clr
  Register #(.width(16)) register_9 (
    .D(reg_guar), .en(demultiplexer_1_out10), .Q(register_9_q), .clk(cloc));  // open: clr
  Register #(.width(16)) register_10 (
    .D(reg_guar), .en(demultiplexer_1_out11), .Q(register_10_q), .clk(cloc));  // open: clr
  Register #(.width(16)) register_11 (
    .D(reg_guar), .en(demultiplexer_1_out8), .Q(register_11_q), .clk(cloc));  // open: clr
  Register #(.width(16)) register_12 (
    .D(reg_guar), .en(demultiplexer_1_out12), .Q(register_12_q), .clk(cloc));  // open: clr
  Register #(.width(16)) register_13 (
    .D(reg_guar), .en(demultiplexer_1_out13), .Q(register_13_q), .clk(cloc));  // open: clr
  Register #(.width(16)) register_14 (
    .D(reg_guar), .en(demultiplexer_1_out14), .Q(register_14_q), .clk(cloc));  // open: clr
  Register #(.width(16)) register_15 (
    .D(reg_guar), .en(demultiplexer_1_out15), .Q(register_15_q), .clk(cloc));  // open: clr
  Multiplexer #(.select(4), .width(16)) multiplexer_1 (
    .in0({16{1'b0}}), .in1(register_1_q), .in2(register_2_q), .in3(register_3_q), .in4(register_4_q),
    .in5(register_5_q), .in6(register_6_q), .in7(register_7_q), .in8(register_11_q), .in9(register_8_q),
    .in10(register_9_q), .in11(register_10_q), .in12(register_12_q), .in13(register_13_q),
    .in14(register_14_q), .in15(register_15_q), .out(reg_1), .sel(eleg_reg_1), .en(on_off));
  Multiplexer #(.select(4), .width(16)) multiplexer_2 (
    .in0({16{1'b0}}), .in1(register_1_q), .in2(register_2_q), .in3(register_3_q), .in4(register_4_q),
    .in5(register_5_q), .in6(register_6_q), .in7(register_7_q), .in8(register_11_q), .in9(register_8_q),
    .in10(register_9_q), .in11(register_10_q), .in12(register_12_q), .in13(register_13_q),
    .in14(register_14_q), .in15(register_15_q), .out(reg_2), .sel(eleg_reg_2), .en(on_off));
endmodule

module ALU (
  input  [15:0] reg_A,
  input  [15:0] Reg_B,
  input  [15:0] off_on,
  output [15:0] Reg_Dest,
  output BRANHC
);

  wire comparator_1_lt, comparator_2_eq, comparator_2_lt, comparator_3_eq, comparator_4_eq, or_2_out;
  wire [0:0] undriven, undriven_2;
  wire [15:0] adder_1_out, and_1_out, or_1_out, shifter_1_out, subtractor_1_out, xor_1_out;

  Comparator #(.width(4), .mode("unsigned")) comparator_1 (
    .a(off_on[3:0]), .b(4'b1010), .lt(comparator_1_lt));  // open: gt, eq
  Adder #(.width(16)) adder_1 (.a(reg_A), .b(Reg_B), .out(adder_1_out));  // open: cin, cout
  Subtractor #(.width(16)) subtractor_1 (.a(reg_A), .b(Reg_B), .out(subtractor_1_out));  // open: bin, bout
  assign and_1_out = reg_A & Reg_B;  // AND_Gate and_1, 16 bits wide
  assign or_1_out = reg_A | Reg_B;  // OR_Gate or_1, 16 bits wide
  assign xor_1_out = reg_A ^ Reg_B;  // XOR_Gate xor_1, 16 bits wide
  Shifter #(.width(16)) shifter_1 (.in(reg_A), .\dist (4'b0001), .out(shifter_1_out));
  Comparator #(.width(16)) comparator_2 (.a(reg_A), .b(Reg_B), .eq(comparator_2_eq), .lt(comparator_2_lt));  // open: gt
  Comparator #(.width(3)) comparator_3 (.a(off_on[2:0]), .b(3'b110), .eq(comparator_3_eq));  // open: gt, lt
  Comparator #(.width(3)) comparator_4 (.a(off_on[2:0]), .b(3'b111), .eq(comparator_4_eq));  // open: gt, lt
  Hex_Digit_Display hex_digit_display_1 (.value(Reg_Dest[11:8]), .dp(comparator_1_lt));
  Hex_Digit_Display hex_digit_display_2 (.value(Reg_Dest[15:12]), .dp(comparator_1_lt));
  Multiplexer #(.select(3), .width(16)) multiplexer_1 (
    .in0(adder_1_out), .in1(subtractor_1_out), .in2(and_1_out), .in3(or_1_out), .in4(xor_1_out),
    .in5(shifter_1_out), .in6({{15{1'b0}}, undriven[0]}), .in7({{15{1'b0}}, undriven_2[0]}), .out(Reg_Dest),
    .sel(off_on[2:0]), .en(comparator_1_lt));
  Hex_Digit_Display hex_digit_display_3 (.value(Reg_Dest[7:4]), .dp(comparator_1_lt));
  or or_2 (or_2_out, comparator_3_eq, comparator_4_eq);
  Hex_Digit_Display hex_digit_display_4 (.value(Reg_Dest[3:0]), .dp(comparator_1_lt));
  Multiplexer multiplexer_2 (
    .in0(comparator_2_lt), .in1(comparator_2_eq), .out(BRANHC), .sel(comparator_4_eq), .en(or_2_out));
endmodule

module lilui (
  input  [15:0] entrada,
  output [15:0] imedia
);

  wire comparator_1_eq, comparator_2_eq, or_1_out;
  wire [15:0] bit_extender_1_out;

  assign bit_extender_1_out = {{8{entrada[15]}}, entrada[15:8]};  // Bit_Extender bit_extender_1
  Comparator #(.width(4)) comparator_1 (.a(entrada[3:0]), .b(4'b1010), .eq(comparator_1_eq));  // open: gt, lt
  Comparator #(.width(4)) comparator_2 (.a(entrada[3:0]), .b(4'b1011), .eq(comparator_2_eq));  // open: gt, lt
  Multiplexer #(.width(16)) multiplexer_1 (
    .in0(bit_extender_1_out), .in1({entrada[15:8], {8{1'b0}}}), .out(imedia), .sel(entrada[0]), .en(or_1_out));
  or or_1 (or_1_out, comparator_1_eq, comparator_2_eq);
endmodule

module jump (
  input  [15:0] ram,
  input  [15:0] pc,
  input  [15:0] \reg ,
  output [3:0] sal_reg,
  output [15:0] salida
);

  wire [0:0] comparator_1_eq, comparator_2_eq;
  wire [1:0] adder_1_out, multiplexer_1_out;
  wire [15:0] bit_extender_1_out, undriven;

  assign bit_extender_1_out = {{8{ram[15]}}, ram[15:8]};  // Bit_Extender bit_extender_1
  Comparator #(.width(4)) comparator_1 (.a(ram[3:0]), .b(4'b1110), .eq(comparator_1_eq[0]));  // open: gt, lt
  Comparator #(.width(4)) comparator_2 (.a(ram[3:0]), .b(4'b1100), .eq(comparator_2_eq[0]));  // open: gt, lt
  Multiplexer #(.width(2)) multiplexer_1 (
    .in0({1'b0, comparator_2_eq[0]}), .in1(adder_1_out), .out(multiplexer_1_out), .sel(comparator_1_eq[0]));  // open: en
  Multiplexer #(.select(2), .width(16)) multiplexer_2 (
    .in0(pc), .in1(bit_extender_1_out), .in2(\reg ), .in3(undriven), .out(salida), .sel(multiplexer_1_out));  // open: en
  Multiplexer #(.width(4)) multiplexer_3 (.in1(ram[11:8]), .out(sal_reg), .sel(comparator_1_eq[0]));  // open: in0, en
  Adder #(.width(2)) adder_1 (.a({1'b0, comparator_1_eq[0]}), .b(2'b01), .out(adder_1_out));  // open: cin, cout
endmodule

module cambio (
  input  [15:0] entrada,
  output [15:0] out_2
);


  assign out_2 = {entrada[3:0], entrada[7:4], entrada[11:8], entrada[15:12]};
endmodule

module brnach (
  input  [15:0] inm,
  input  [15:0] pc,
  input  [15:0] sum,
  input  bitbranch,
  output [15:0] salida
);

  wire comparator_1_eq, comparator_2_eq, comparator_3_eq, comparator_4_eq, not_1_out;
  wire [15:0] adder_1_out, bit_extender_1_out, demultiplexer_1_out1;

  assign bit_extender_1_out = {{8{inm[15]}}, inm[15:8]};  // Bit_Extender bit_extender_1
  Adder #(.width(16)) adder_1 (.a(bit_extender_1_out), .b(pc), .out(adder_1_out));  // open: cin, cout
  Demultiplexer #(.width(16)) demultiplexer_1 (
    .out0(salida), .out1(demultiplexer_1_out1), .in(sum), .sel(comparator_4_eq), .en(not_1_out));
  not not_1 (not_1_out, comparator_4_eq);
  Comparator #(.width(1)) comparator_1 (.a(bitbranch), .b(1'b0), .eq(comparator_1_eq));  // open: gt, lt
  assign salida = comparator_2_eq ? sum : 16'bz;  // Controlled_Buffer controlled_buffer_1
  Comparator #(.width(1)) comparator_2 (
    .a(comparator_1_eq), .b(comparator_3_eq), .eq(comparator_2_eq));  // open: gt, lt
  Multiplexer #(.width(16)) multiplexer_1 (
    .in0(demultiplexer_1_out1), .in1(adder_1_out), .out(salida), .sel(bitbranch), .en(comparator_4_eq));
  Comparator #(.width(1)) comparator_3 (.a(1'b1), .b(comparator_4_eq), .eq(comparator_3_eq));  // open: gt, lt
  Comparator #(.width(4)) comparator_4 (.a(inm[3:0]), .b(4'b1101), .eq(comparator_4_eq));  // open: gt, lt
endmodule
